// Logisim project proutiti.circ as structural Verilog: 3 circuits, main circuit main
module main (
  input  [7:0] B,
  input  [7:0] A,
  output [3:0] P
);

  and A0B0 (P[0], B[0], A[0]);
  // AND_Gate A0B1 has open pins: in0=B[1], in1=A[0], out=open
  // AND_Gate A1B0 has open pins: in0=B[0], in1=A[1], out=open
  // AND_Gate A0B2 has open pins: in0=A[0], in1=B[2], out=open
  // AND_Gate A1B1 has open pins: in0=A[1], in1=B[1], out=open
  // AND_Gate A2B0 has open pins: in0=A[2], in1=B[0], out=open
  // AND_Gate A0B3 has open pins: in0=A[0], in1=B[3], out=open
  // AND_Gate A1B2 has open pins: in0=A[1], in1=B[2], out=open
  // AND_Gate A2B1 has open pins: in0=A[2], in1=B[1], out=open
  // AND_Gate A3B0 has open pins: in0=A[3], in1=B[0], out=open
endmodule

module HaAdd (
  input  A,
  input  B,
  output S,
  output R
);

  xor xor_1 (S, A, B);
  and and_1 (R, A, B);
endmodule

module FuAdd (
  input  A,
  input  B,
  input  R,
  output S,
  output Res
);

  wire haadd_1_r, haadd_1_s, haadd_2_r;

  HaAdd haadd_1 (.A(B), .B(R), .S(haadd_1_s), .R(haadd_1_r));
  HaAdd haadd_2 (.A(A), .B(haadd_1_s), .S(S), .R(haadd_2_r));
  or or_1 (Res, haadd_2_r, haadd_1_r);
endmodule
